# Fritzing sketch board (saved by Fritzing 0.9.9b)
perfboards: 1

parts:
  IC1 = IC, DIP package, 14 pins [chip_label=PIC16LF1613-I/P]
  IC2 = IC, DIP package, 14 pins [chip_label=PIC16LF1613-I/P]
  IC3 = IC, DIP package, 14 pins [chip_label=PIC16LF1613-I/P]
  IC4 = IC, DIP package, 14 pins [chip_label=PIC16LF1613-I/P]
  U1 = LM 358 Dual Op-Amp [package="DIP8 [THT]"]
  R1 = Dial Potentiometer with switch [maximum_resistance=100kΩ]
  TRS1 = Audio Jack (TRS) 3.5mm [package="4Ucon 08780 [THT]"]
  HEF1 = HEF4094 [package="DIP16 [THT]"]
  DATA = male pin header, 8 pins [form="♂ (male)"]
  CONTROL = male pin header, 4 pins [form="♂ (male)"]
  POWER = male pin header, 2 pins [form="♂ (male)"]

nets:
  N1: IC1.pin1, IC2.pin1, IC3.pin1, IC4.pin1, U1.connector7, HEF1.OE, HEF1.Vdd, POWER.pin1
  N2: IC1.pin2, IC2.pin2, IC3.pin2, IC4.pin2, DATA.pin1
  N3: IC1.pin3, IC2.pin3, IC3.pin3, IC4.pin3, DATA.pin2
  N4: IC1.pin5, IC2.pin5, IC3.pin5, IC4.pin5, DATA.pin3
  N5: IC1.pin6, IC2.pin6, IC3.pin6, IC4.pin6, DATA.pin4
  N6: IC1.pin7, IC2.pin7, IC3.pin7, IC4.pin7, DATA.pin5
  N7: IC1.pin8, IC2.pin8, IC3.pin8, IC4.pin8, DATA.pin6
  N8: IC1.pin9, IC2.pin9, IC3.pin9, IC4.pin9, DATA.pin7
  N9: IC1.pin10, IC2.pin10, IC3.pin10, IC4.pin10, DATA.pin8
  N10: IC1.pin11, HEF1.Q1
  N11: IC1.pin12, IC2.pin12, IC3.pin12, IC4.pin12, CONTROL.pin4
  N12: IC1.pin13, IC2.pin13, IC3.pin13, IC4.pin13, U1.connector5, R1.leg2
  N13: IC1.pin14, IC2.pin14, IC3.pin14, IC4.pin14, R1.leg1, R1.switch_leg1, HEF1.Vss, POWER.pin2
  N14: IC2.pin11, HEF1.Q2
  N15: IC3.pin11, HEF1.Q3
  N16: IC4.pin11, HEF1.Q4
  N17: U1.connector3, U1.connector4, TRS1.Sleeve
  N18: U1.connector6, R1.switch_leg2, TRS1.Ring, TRS1.Tip
  N19: HEF1.STROBE, CONTROL.pin1
  N20: HEF1.DATA, CONTROL.pin2
  N21: HEF1.CLOCK, CONTROL.pin3
